# Fritzing sketch robut (saved by Fritzing 0.8.0b)
breadboards: 1

parts:
  Teensy1 = Teensy 2.0
  Part1 = 9 Degrees of Freedom - Sensor Stick
  J1 = Basic Servo
  J2 = Basic Servo
  U1 = Voltage Regulator - 5V [package="DPak [SMD]"]
  S1 = Toggle Switch [package=THT]
  VCC1 = Battery block 9V

nets:
  GND: Teensy1.GND, J1.gnd, J2.gnd, U1.GND, VCC1.-
  N1: Teensy1.D0, Part1.SCL
  N2: Teensy1.D1, Part1.SDA
  N3: Teensy1.C7, J2.pulse
  VCC: Teensy1.VCC, Part1.VCC, J2.vcc, U1.output_voltage
  N4: Teensy1.D7, J1.pulse
  N5: U1.input_voltage, S1.L1
  N6: S1.COM, VCC1.+
